// Logisim project Circuit.circ as structural Verilog: 6 circuits, main circuit main
module main (
  input  in_1,
  input  A0,
  input  A1,
  input  B0,
  input  A2,
  input  B1,
  input  A3,
  input  B2,
  input  A4,
  input  B3,
  input  A5,
  input  B4,
  input  A6,
  input  B5,
  input  A7,
  input  B6,
  input  B7
);

  wire Clk_out, controlunit_1_ea, controlunit_1_eb, controlunit_1_ep, controlunit_1_la, controlunit_1_lb,
       controlunit_1_psel, controlunit_1_rstp, nor_1_out, shiftrightreg_1_out_0, shiftrightreg_1_out_1,
       shiftrightreg_1_out_2, shiftrightreg_1_out_3, shiftrightreg_1_out_4, shiftrightreg_1_out_5,
       shiftrightreg_1_out_6, shiftrightreg_1_out_7, xor_1_out;
  wire [7:0] eightbit2compliment_1_o0, eightbit2compliment_2_o0, multiplexer_1_out, multiplexer_3_out;
  wire [15:0] adder_1_out, multiplexer_2_out, preg_1_out_0, shiftleftreg_1_out_0;

  xor xor_1 (xor_1_out, A7, B7);
  eightbit2compliment eightbit2compliment_1 (
    .I7(A7), .I6(A6), .I5(A5), .I4(A4), .I3(A3), .I2(A2), .I1(A1), .I0(A0), .O0(eightbit2compliment_1_o0[0]),
    .O7(eightbit2compliment_1_o0[7]), .O6(eightbit2compliment_1_o0[6]), .O5(eightbit2compliment_1_o0[5]),
    .O4(eightbit2compliment_1_o0[4]), .O3(eightbit2compliment_1_o0[3]), .O2(eightbit2compliment_1_o0[2]),
    .O1(eightbit2compliment_1_o0[1]));
  Adder #(.width(16)) adder_1 (.a(shiftleftreg_1_out_0), .b(preg_1_out_0), .out(adder_1_out));  // open: cin, cout
  Multiplexer #(.width(8)) multiplexer_1 (
    .in0({A7, A6, A5, A4, A3, A2, A1, A0}), .in1(eightbit2compliment_1_o0), .out(multiplexer_1_out), .sel(A7));
  shiftLeftReg shiftleftreg_1 (
    .I_0(multiplexer_1_out[0]), .I_1(multiplexer_1_out[1]), .i_2(multiplexer_1_out[2]),
    .I_3(multiplexer_1_out[3]), .I_4(multiplexer_1_out[4]), .I_5(multiplexer_1_out[5]),
    .I_6(multiplexer_1_out[6]), .i_7(multiplexer_1_out[7]), .Clock(Clk_out), .Enable(controlunit_1_ea),
    .Load(controlunit_1_la), .Out_0(shiftleftreg_1_out_0[0]), .Out_1(shiftleftreg_1_out_0[1]),
    .Out_2(shiftleftreg_1_out_0[2]), .Out_3(shiftleftreg_1_out_0[3]), .Out_4(shiftleftreg_1_out_0[4]),
    .Out_5(shiftleftreg_1_out_0[5]), .Out_6(shiftleftreg_1_out_0[6]), .Out_7(shiftleftreg_1_out_0[7]),
    .Out_8(shiftleftreg_1_out_0[8]), .Out_9(shiftleftreg_1_out_0[9]), .Out_10(shiftleftreg_1_out_0[10]),
    .Out_11(shiftleftreg_1_out_0[11]), .Out_12(shiftleftreg_1_out_0[12]), .Out_13(shiftleftreg_1_out_0[13]),
    .Out_14(shiftleftreg_1_out_0[14]), .Out_15(shiftleftreg_1_out_0[15]));
  Clock Clk (.out(Clk_out));
  Multiplexer #(.width(16)) multiplexer_2 (
    .in0({16{1'b0}}), .in1(adder_1_out), .out(multiplexer_2_out), .sel(controlunit_1_psel));
  PReg preg_1 (
    .I_0(multiplexer_2_out[0]), .I_1(multiplexer_2_out[1]), .I_2(multiplexer_2_out[2]),
    .I_3(multiplexer_2_out[3]), .I_4(multiplexer_2_out[4]), .I_5(multiplexer_2_out[5]),
    .I_6(multiplexer_2_out[6]), .I_7(multiplexer_2_out[7]), .I_8(multiplexer_2_out[8]),
    .I_9(multiplexer_2_out[9]), .I_10(multiplexer_2_out[10]), .I_11(multiplexer_2_out[11]),
    .I_12(multiplexer_2_out[12]), .I_13(multiplexer_2_out[13]), .I_14(multiplexer_2_out[14]),
    .I_15(multiplexer_2_out[15]), .Clock(Clk_out), .Reset(controlunit_1_rstp), .Load(controlunit_1_ep),
    .Out_0(preg_1_out_0[0]), .Out_1(preg_1_out_0[1]), .Out_2(preg_1_out_0[2]), .Out_3(preg_1_out_0[3]),
    .Out_4(preg_1_out_0[4]), .Out_5(preg_1_out_0[5]), .Out_6(preg_1_out_0[6]), .Out_7(preg_1_out_0[7]),
    .Out_8(preg_1_out_0[8]), .Out_9(preg_1_out_0[9]), .Out_10(preg_1_out_0[10]), .Out_11(preg_1_out_0[11]),
    .Out_12(preg_1_out_0[12]), .Out_13(preg_1_out_0[13]), .Out_14(preg_1_out_0[14]), .Out_15(preg_1_out_0[15]));
  shiftRightReg shiftrightreg_1 (
    .i_0(multiplexer_3_out[0]), .I_1(multiplexer_3_out[1]), .I_2(multiplexer_3_out[2]),
    .I_3(multiplexer_3_out[3]), .I_4(multiplexer_3_out[4]), .I_5(multiplexer_3_out[5]),
    .I_6(multiplexer_3_out[6]), .i_7(multiplexer_3_out[7]), .Clock(Clk_out), .Enable(controlunit_1_eb),
    .Load(controlunit_1_lb), .Out_0(shiftrightreg_1_out_0), .Out_1(shiftrightreg_1_out_1),
    .Out_2(shiftrightreg_1_out_2), .Out_3(shiftrightreg_1_out_3), .Out_4(shiftrightreg_1_out_4),
    .Out_5(shiftrightreg_1_out_5), .Out_6(shiftrightreg_1_out_6), .Out_7(shiftrightreg_1_out_7));
  eightbit2compliment eightbit2compliment_2 (
    .I7(B7), .I6(B6), .I5(B5), .I4(B4), .I3(B3), .I2(B2), .I1(B1), .I0(B0), .O0(eightbit2compliment_2_o0[0]),
    .O7(eightbit2compliment_2_o0[7]), .O6(eightbit2compliment_2_o0[6]), .O5(eightbit2compliment_2_o0[5]),
    .O4(eightbit2compliment_2_o0[4]), .O3(eightbit2compliment_2_o0[3]), .O2(eightbit2compliment_2_o0[2]),
    .O1(eightbit2compliment_2_o0[1]));
  nor nor_1 (nor_1_out, shiftrightreg_1_out_7, shiftrightreg_1_out_6, shiftrightreg_1_out_5, shiftrightreg_1_out_4, shiftrightreg_1_out_3, shiftrightreg_1_out_2, shiftrightreg_1_out_1, shiftrightreg_1_out_0);
  LED led_1 (.in(preg_1_out_0[0]));
  LED led_2 (.in(preg_1_out_0[0]));
  LED led_3 (.in(preg_1_out_0[1]));
  LED led_4 (.in(preg_1_out_0[2]));
  LED led_5 (.in(preg_1_out_0[2]));
  LED led_6 (.in(preg_1_out_0[3]));
  LED led_7 (.in(preg_1_out_0[3]));
  LED led_8 (.in(preg_1_out_0[4]));
  LED led_9 (.in(preg_1_out_0[4]));
  LED led_10 (.in(preg_1_out_0[5]));
  LED led_11 (.in(preg_1_out_0[5]));
  LED led_12 (.in(preg_1_out_0[6]));
  LED led_13 (.in(preg_1_out_0[7]));
  LED led_14 (.in(preg_1_out_0[7]));
  LED led_15 (.in(preg_1_out_0[8]));
  LED led_16 (.in(preg_1_out_0[9]));
  LED led_17 (.in(preg_1_out_0[9]));
  LED led_18 (.in(preg_1_out_0[10]));
  LED led_19 (.in(preg_1_out_0[10]));
  LED led_20 (.in(preg_1_out_0[11]));
  LED led_21 (.in(preg_1_out_0[12]));
  LED led_22 (.in(preg_1_out_0[12]));
  LED led_23 (.in(preg_1_out_0[13]));
  LED led_24 (.in(preg_1_out_0[13]));
  LED led_25 (.in(preg_1_out_0[14]));
  LED led_26 (.in(preg_1_out_0[14]));
  LED led_27 (.in(preg_1_out_0[15]));
  LED led_28 (.in(preg_1_out_0[15]));
  LED Out_Sign (.in(xor_1_out));
  LED Out_Sign_1 (.in(xor_1_out));
  ControlUnit controlunit_1 (
    .B0(shiftrightreg_1_out_0), .Z(nor_1_out), .Load(in_1), .Psel(controlunit_1_psel), .EP(controlunit_1_ep),
    .EA(controlunit_1_ea), .EB(controlunit_1_eb), .LA(controlunit_1_la), .LB(controlunit_1_lb),
    .RstP(controlunit_1_rstp));
  Multiplexer #(.width(8)) multiplexer_3 (
    .in0({B7, B6, B5, B4, B3, B2, B1, B0}), .in1(eightbit2compliment_2_o0), .out(multiplexer_3_out), .sel(B7));
  LED Mul_Finished (.in(nor_1_out));
endmodule

module eightbit2compliment (
  input  I0,
  input  I1,
  input  I2,
  input  I3,
  input  I4,
  input  I5,
  input  I6,
  input  I7,
  output O0,
  output O1,
  output O2,
  output O3,
  output O4,
  output O5,
  output O6,
  output O7
);

  wire adder_2_cout, adder_3_cout, adder_4_cout, adder_5_cout, adder_6_cout, adder_7_cout, adder_8_cout,
       not_1_out, not_2_out, not_3_out, not_4_out, not_5_out, not_6_out, not_7_out, not_8_out;

  not not_1 (not_1_out, I7);
  not not_2 (not_2_out, I6);
  Adder #(.width(1)) adder_1 (.a(not_1_out), .b(adder_2_cout), .out(O7));  // open: cin, cout
  not not_3 (not_3_out, I5);
  Adder #(.width(1)) adder_2 (.a(not_2_out), .b(adder_3_cout), .out(O6), .cout(adder_2_cout));  // open: cin
  not not_4 (not_4_out, I4);
  Adder #(.width(1)) adder_3 (.a(not_3_out), .b(adder_4_cout), .out(O5), .cout(adder_3_cout));  // open: cin
  Adder #(.width(1)) adder_4 (.a(not_4_out), .b(adder_5_cout), .out(O4), .cout(adder_4_cout));  // open: cin
  not not_5 (not_5_out, I3);
  Adder #(.width(1)) adder_5 (.a(not_5_out), .b(adder_6_cout), .out(O3), .cout(adder_5_cout));  // open: cin
  not not_6 (not_6_out, I2);
  Adder #(.width(1)) adder_6 (.a(not_6_out), .b(adder_7_cout), .out(O2), .cout(adder_6_cout));  // open: cin
  not not_7 (not_7_out, I1);
  Adder #(.width(1)) adder_7 (.a(not_7_out), .b(adder_8_cout), .out(O1), .cout(adder_7_cout));  // open: cin
  not not_8 (not_8_out, I0);
  Adder #(.width(1)) adder_8 (.a(not_8_out), .b(1'b1), .out(O0), .cout(adder_8_cout));  // open: cin
endmodule

// reg
module shiftRightReg (
  input  i_0,
  input  I_1,
  input  I_2,
  input  I_3,
  input  I_4,
  input  I_5,
  input  I_6,
  input  i_7,
  input  Clock,
  input  Enable,
  input  Load,
  output Out_0,
  output Out_1,
  output Out_2,
  output Out_3,
  output Out_4,
  output Out_5,
  output Out_6,
  output Out_7
);

  wire multiplexer_1_out, multiplexer_2_out, multiplexer_3_out, multiplexer_4_out, multiplexer_5_out,
       multiplexer_6_out, multiplexer_7_out, multiplexer_8_out, multiplexer_9_out, multiplexer_10_out,
       multiplexer_11_out, multiplexer_12_out, multiplexer_13_out, multiplexer_14_out, multiplexer_15_out,
       multiplexer_16_out, undriven, undriven_2, undriven_3, undriven_4, undriven_5, undriven_6, undriven_7,
       undriven_8;

  Multiplexer multiplexer_1 (.in0(1'b0), .in1(i_7), .out(multiplexer_1_out), .sel(Load));
  D_Flip_Flop d_ff_1 (.D(multiplexer_2_out), .clk(Clock), .Q(Out_7), .reset(undriven));  // open: Qn, preset
  Multiplexer multiplexer_2 (.in0(Out_7), .in1(multiplexer_1_out), .out(multiplexer_2_out), .sel(Enable));
  Multiplexer multiplexer_3 (.in0(Out_7), .in1(I_6), .out(multiplexer_3_out), .sel(Load));
  D_Flip_Flop d_ff_2 (.D(multiplexer_4_out), .clk(Clock), .Q(Out_6), .reset(undriven_2));  // open: Qn, preset
  Multiplexer multiplexer_4 (.in0(Out_6), .in1(multiplexer_3_out), .out(multiplexer_4_out), .sel(Enable));
  Multiplexer multiplexer_5 (.in0(Out_6), .in1(I_5), .out(multiplexer_5_out), .sel(Load));
  Multiplexer multiplexer_6 (.in0(Out_5), .in1(multiplexer_5_out), .out(multiplexer_6_out), .sel(Enable));
  D_Flip_Flop d_ff_3 (.D(multiplexer_6_out), .clk(Clock), .Q(Out_5), .reset(undriven_3));  // open: Qn, preset
  Multiplexer multiplexer_7 (.in0(Out_5), .in1(I_4), .out(multiplexer_7_out), .sel(Load));
  Multiplexer multiplexer_8 (.in0(Out_4), .in1(multiplexer_7_out), .out(multiplexer_8_out), .sel(Enable));
  D_Flip_Flop d_ff_4 (.D(multiplexer_8_out), .clk(Clock), .Q(Out_4), .reset(undriven_4));  // open: Qn, preset
  Multiplexer multiplexer_9 (.in0(Out_4), .in1(I_3), .out(multiplexer_9_out), .sel(Load));
  Multiplexer multiplexer_10 (.in0(Out_3), .in1(multiplexer_9_out), .out(multiplexer_10_out), .sel(Enable));
  D_Flip_Flop d_ff_5 (.D(multiplexer_10_out), .clk(Clock), .Q(Out_3), .reset(undriven_5));  // open: Qn, preset
  Multiplexer multiplexer_11 (.in0(Out_3), .in1(I_2), .out(multiplexer_11_out), .sel(Load));
  Multiplexer multiplexer_12 (.in0(Out_2), .in1(multiplexer_11_out), .out(multiplexer_12_out), .sel(Enable));
  D_Flip_Flop d_ff_6 (.D(multiplexer_12_out), .clk(Clock), .Q(Out_2), .reset(undriven_6));  // open: Qn, preset
  Multiplexer multiplexer_13 (.in0(Out_2), .in1(I_1), .out(multiplexer_13_out), .sel(Load));
  Multiplexer multiplexer_14 (.in0(Out_1), .in1(multiplexer_13_out), .out(multiplexer_14_out), .sel(Enable));
  D_Flip_Flop d_ff_7 (.D(multiplexer_14_out), .clk(Clock), .Q(Out_1), .reset(undriven_7));  // open: Qn, preset
  Multiplexer multiplexer_15 (.in0(Out_1), .in1(i_0), .out(multiplexer_15_out), .sel(Load));
  Multiplexer multiplexer_16 (.in0(Out_0), .in1(multiplexer_15_out), .out(multiplexer_16_out), .sel(Enable));
  D_Flip_Flop d_ff_8 (.D(multiplexer_16_out), .clk(Clock), .Q(Out_0), .reset(undriven_8));  // open: Qn, preset
endmodule

module shiftLeftReg (
  input  I_0,
  input  I_1,
  input  i_2,
  input  I_3,
  input  I_4,
  input  I_5,
  input  I_6,
  input  i_7,
  input  Clock,
  input  Enable,
  input  Load,
  output Out_0,
  output Out_1,
  output Out_2,
  output Out_3,
  output Out_4,
  output Out_5,
  output Out_6,
  output Out_7,
  output Out_8,
  output Out_9,
  output Out_10,
  output Out_11,
  output Out_12,
  output Out_13,
  output Out_14,
  output Out_15
);

  wire multiplexer_1_out, multiplexer_2_out, multiplexer_3_out, multiplexer_4_out, multiplexer_5_out,
       multiplexer_6_out, multiplexer_7_out, multiplexer_8_out, multiplexer_9_out, multiplexer_10_out,
       multiplexer_11_out, multiplexer_12_out, multiplexer_13_out, multiplexer_14_out, multiplexer_15_out,
       multiplexer_16_out, multiplexer_17_out, multiplexer_18_out, multiplexer_19_out, multiplexer_20_out,
       multiplexer_21_out, multiplexer_22_out, multiplexer_23_out, multiplexer_24_out, multiplexer_25_out,
       multiplexer_26_out, multiplexer_27_out, multiplexer_28_out, multiplexer_29_out, multiplexer_30_out,
       multiplexer_31_out, multiplexer_32_out, undriven, undriven_2, undriven_3, undriven_4, undriven_5,
       undriven_6, undriven_7, undriven_8, undriven_9, undriven_10, undriven_11, undriven_12, undriven_13,
       undriven_14, undriven_15, undriven_16;

  Multiplexer multiplexer_1 (.in0(Out_14), .in1(1'b0), .out(multiplexer_1_out), .sel(Load));
  Multiplexer multiplexer_2 (.in0(Out_6), .in1(i_7), .out(multiplexer_2_out), .sel(Load));
  D_Flip_Flop d_ff_1 (.D(multiplexer_3_out), .clk(Clock), .Q(Out_15), .reset(undriven));  // open: Qn, preset
  Multiplexer multiplexer_3 (.in0(Out_15), .in1(multiplexer_1_out), .out(multiplexer_3_out), .sel(Enable));
  D_Flip_Flop d_ff_2 (.D(multiplexer_4_out), .clk(Clock), .Q(Out_7), .reset(undriven_2));  // open: Qn, preset
  Multiplexer multiplexer_4 (.in0(Out_7), .in1(multiplexer_2_out), .out(multiplexer_4_out), .sel(Enable));
  Multiplexer multiplexer_5 (.in0(Out_13), .in1(1'b0), .out(multiplexer_5_out), .sel(Load));
  Multiplexer multiplexer_6 (.in0(Out_5), .in1(I_6), .out(multiplexer_6_out), .sel(Load));
  D_Flip_Flop d_ff_3 (.D(multiplexer_7_out), .clk(Clock), .Q(Out_14), .reset(undriven_3));  // open: Qn, preset
  Multiplexer multiplexer_7 (.in0(Out_14), .in1(multiplexer_5_out), .out(multiplexer_7_out), .sel(Enable));
  D_Flip_Flop d_ff_4 (.D(multiplexer_8_out), .clk(Clock), .Q(Out_6), .reset(undriven_4));  // open: Qn, preset
  Multiplexer multiplexer_8 (.in0(Out_6), .in1(multiplexer_6_out), .out(multiplexer_8_out), .sel(Enable));
  Multiplexer multiplexer_9 (.in0(Out_12), .in1(1'b0), .out(multiplexer_9_out), .sel(Load));
  Multiplexer multiplexer_10 (.in0(Out_4), .in1(I_5), .out(multiplexer_10_out), .sel(Load));
  Multiplexer multiplexer_11 (.in0(Out_13), .in1(multiplexer_9_out), .out(multiplexer_11_out), .sel(Enable));
  Multiplexer multiplexer_12 (.in0(Out_5), .in1(multiplexer_10_out), .out(multiplexer_12_out), .sel(Enable));
  D_Flip_Flop d_ff_5 (.D(multiplexer_11_out), .clk(Clock), .Q(Out_13), .reset(undriven_5));  // open: Qn, preset
  D_Flip_Flop d_ff_6 (.D(multiplexer_12_out), .clk(Clock), .Q(Out_5), .reset(undriven_6));  // open: Qn, preset
  Multiplexer multiplexer_13 (.in0(Out_11), .in1(1'b0), .out(multiplexer_13_out), .sel(Load));
  Multiplexer multiplexer_14 (.in0(Out_12), .in1(multiplexer_13_out), .out(multiplexer_14_out), .sel(Enable));
  Multiplexer multiplexer_15 (.in0(Out_3), .in1(I_4), .out(multiplexer_15_out), .sel(Load));
  Multiplexer multiplexer_16 (.in0(Out_4), .in1(multiplexer_15_out), .out(multiplexer_16_out), .sel(Enable));
  D_Flip_Flop d_ff_7 (.D(multiplexer_14_out), .clk(Clock), .Q(Out_12), .reset(undriven_7));  // open: Qn, preset
  D_Flip_Flop d_ff_8 (.D(multiplexer_16_out), .clk(Clock), .Q(Out_4), .reset(undriven_8));  // open: Qn, preset
  Multiplexer multiplexer_17 (.in0(Out_10), .in1(1'b0), .out(multiplexer_17_out), .sel(Load));
  Multiplexer multiplexer_18 (.in0(Out_11), .in1(multiplexer_17_out), .out(multiplexer_18_out), .sel(Enable));
  Multiplexer multiplexer_19 (.in0(Out_2), .in1(I_3), .out(multiplexer_19_out), .sel(Load));
  Multiplexer multiplexer_20 (.in0(Out_3), .in1(multiplexer_19_out), .out(multiplexer_20_out), .sel(Enable));
  D_Flip_Flop d_ff_9 (.D(multiplexer_18_out), .clk(Clock), .Q(Out_11), .reset(undriven_9));  // open: Qn, preset
  D_Flip_Flop d_ff_10 (.D(multiplexer_20_out), .clk(Clock), .Q(Out_3), .reset(undriven_10));  // open: Qn, preset
  Multiplexer multiplexer_21 (.in0(Out_9), .in1(1'b0), .out(multiplexer_21_out), .sel(Load));
  Multiplexer multiplexer_22 (.in0(Out_1), .in1(i_2), .out(multiplexer_22_out), .sel(Load));
  Multiplexer multiplexer_23 (.in0(Out_10), .in1(multiplexer_21_out), .out(multiplexer_23_out), .sel(Enable));
  Multiplexer multiplexer_24 (.in0(Out_2), .in1(multiplexer_22_out), .out(multiplexer_24_out), .sel(Enable));
  D_Flip_Flop d_ff_11 (.D(multiplexer_23_out), .clk(Clock), .Q(Out_10), .reset(undriven_11));  // open: Qn, preset
  D_Flip_Flop d_ff_12 (.D(multiplexer_24_out), .clk(Clock), .Q(Out_2), .reset(undriven_12));  // open: Qn, preset
  Multiplexer multiplexer_25 (.in0(Out_8), .in1(1'b0), .out(multiplexer_25_out), .sel(Load));
  Multiplexer multiplexer_26 (.in0(Out_9), .in1(multiplexer_25_out), .out(multiplexer_26_out), .sel(Enable));
  Multiplexer multiplexer_27 (.in0(Out_0), .in1(I_1), .out(multiplexer_27_out), .sel(Load));
  Multiplexer multiplexer_28 (.in0(Out_1), .in1(multiplexer_27_out), .out(multiplexer_28_out), .sel(Enable));
  D_Flip_Flop d_ff_13 (.D(multiplexer_26_out), .clk(Clock), .Q(Out_9), .reset(undriven_13));  // open: Qn, preset
  D_Flip_Flop d_ff_14 (.D(multiplexer_28_out), .clk(Clock), .Q(Out_1), .reset(undriven_14));  // open: Qn, preset
  Multiplexer multiplexer_29 (.in0(Out_7), .in1(1'b0), .out(multiplexer_29_out), .sel(Load));
  Multiplexer multiplexer_30 (.in0(1'b0), .in1(I_0), .out(multiplexer_30_out), .sel(Load));
  Multiplexer multiplexer_31 (.in0(Out_8), .in1(multiplexer_29_out), .out(multiplexer_31_out), .sel(Enable));
  Multiplexer multiplexer_32 (.in0(Out_0), .in1(multiplexer_30_out), .out(multiplexer_32_out), .sel(Enable));
  D_Flip_Flop d_ff_15 (.D(multiplexer_31_out), .clk(Clock), .Q(Out_8), .reset(undriven_15));  // open: Qn, preset
  D_Flip_Flop d_ff_16 (.D(multiplexer_32_out), .clk(Clock), .Q(Out_0), .reset(undriven_16));  // open: Qn, preset
endmodule

module ControlUnit (
  input  B0,
  input  Z,
  input  Load,
  output Psel,
  output EP,
  output EA,
  output EB,
  output LA,
  output LB,
  output RstP
);

  wire not_1_out, not_2_out;

  not not_1 (not_1_out, Z);
  or or_1 (EA, not_1_out, Load);
  not not_2 (not_2_out, Load);
  and and_1 (EP, B0, not_2_out);

  assign EB = EA;
  assign LA = Load;
  assign LB = Load;
  assign Psel = B0;
  assign RstP = Load;
endmodule

module PReg (
  input  I_0,
  input  I_1,
  input  I_2,
  input  I_3,
  input  I_4,
  input  I_5,
  input  I_6,
  input  I_7,
  input  I_8,
  input  I_9,
  input  I_10,
  input  I_11,
  input  I_12,
  input  I_13,
  input  I_14,
  input  I_15,
  input  Clock,
  input  Reset,
  input  Load,
  output Out_0,
  output Out_1,
  output Out_2,
  output Out_3,
  output Out_4,
  output Out_5,
  output Out_6,
  output Out_7,
  output Out_8,
  output Out_9,
  output Out_10,
  output Out_11,
  output Out_12,
  output Out_13,
  output Out_14,
  output Out_15
);

  wire multiplexer_1_out, multiplexer_2_out, multiplexer_3_out, multiplexer_4_out, multiplexer_5_out,
       multiplexer_6_out, multiplexer_7_out, multiplexer_8_out, multiplexer_9_out, multiplexer_10_out,
       multiplexer_11_out, multiplexer_12_out, multiplexer_13_out, multiplexer_14_out, multiplexer_15_out,
       multiplexer_16_out;

  Multiplexer multiplexer_1 (.in0(Out_2), .in1(I_2), .out(multiplexer_1_out), .sel(Load));
  Multiplexer multiplexer_2 (.in0(Out_3), .in1(I_3), .out(multiplexer_2_out), .sel(Load));
  Multiplexer multiplexer_3 (.in0(Out_4), .in1(I_4), .out(multiplexer_3_out), .sel(Load));
  Multiplexer multiplexer_4 (.in0(Out_5), .in1(I_5), .out(multiplexer_4_out), .sel(Load));
  Multiplexer multiplexer_5 (.in0(Out_6), .in1(I_6), .out(multiplexer_5_out), .sel(Load));
  Multiplexer multiplexer_6 (.in0(Out_7), .in1(I_7), .out(multiplexer_6_out), .sel(Load));
  Multiplexer multiplexer_7 (.in0(Out_8), .in1(I_8), .out(multiplexer_7_out), .sel(Load));
  Multiplexer multiplexer_8 (.in0(Out_9), .in1(I_9), .out(multiplexer_8_out), .sel(Load));
  Multiplexer multiplexer_9 (.in0(Out_10), .in1(I_10), .out(multiplexer_9_out), .sel(Load));
  Multiplexer multiplexer_10 (.in0(Out_11), .in1(I_11), .out(multiplexer_10_out), .sel(Load));
  Multiplexer multiplexer_11 (.in0(Out_12), .in1(I_12), .out(multiplexer_11_out), .sel(Load));
  Multiplexer multiplexer_12 (.in0(Out_13), .in1(I_13), .out(multiplexer_12_out), .sel(Load));
  Multiplexer multiplexer_13 (.in0(Out_14), .in1(I_14), .out(multiplexer_13_out), .sel(Load));
  Multiplexer multiplexer_14 (.in0(Out_15), .in1(I_15), .out(multiplexer_14_out), .sel(Load));
  Multiplexer multiplexer_15 (.in0(Out_0), .in1(I_0), .out(multiplexer_15_out), .sel(Load));
  D_Flip_Flop d_ff_1 (.D(multiplexer_15_out), .clk(Clock), .Q(Out_0), .reset(Reset));  // open: Qn, preset
  Multiplexer multiplexer_16 (.in0(Out_1), .in1(I_1), .out(multiplexer_16_out), .sel(Load));
  D_Flip_Flop d_ff_2 (.D(multiplexer_16_out), .clk(Clock), .Q(Out_1), .reset(Reset));  // open: Qn, preset
  D_Flip_Flop d_ff_3 (.D(multiplexer_1_out), .clk(Clock), .Q(Out_2), .reset(Reset));  // open: Qn, preset
  D_Flip_Flop d_ff_4 (.D(multiplexer_2_out), .clk(Clock), .Q(Out_3), .reset(Reset));  // open: Qn, preset
  D_Flip_Flop d_ff_5 (.D(multiplexer_3_out), .clk(Clock), .Q(Out_4), .reset(Reset));  // open: Qn, preset
  D_Flip_Flop d_ff_6 (.D(multiplexer_4_out), .clk(Clock), .Q(Out_5), .reset(Reset));  // open: Qn, preset
  D_Flip_Flop d_ff_7 (.D(multiplexer_5_out), .clk(Clock), .Q(Out_6), .reset(Reset));  // open: Qn, preset
  D_Flip_Flop d_ff_8 (.D(multiplexer_6_out), .clk(Clock), .Q(Out_7), .reset(Reset));  // open: Qn, preset
  D_Flip_Flop d_ff_9 (.D(multiplexer_7_out), .clk(Clock), .Q(Out_8), .reset(Reset));  // open: Qn, preset
  D_Flip_Flop d_ff_10 (.D(multiplexer_8_out), .clk(Clock), .Q(Out_9), .reset(Reset));  // open: Qn, preset
  D_Flip_Flop d_ff_11 (.D(multiplexer_9_out), .clk(Clock), .Q(Out_10), .reset(Reset));  // open: Qn, preset
  D_Flip_Flop d_ff_12 (.D(multiplexer_10_out), .clk(Clock), .Q(Out_11), .reset(Reset));  // open: Qn, preset
  D_Flip_Flop d_ff_13 (.D(multiplexer_11_out), .clk(Clock), .Q(Out_12), .reset(Reset));  // open: Qn, preset
  D_Flip_Flop d_ff_14 (.D(multiplexer_12_out), .clk(Clock), .Q(Out_13), .reset(Reset));  // open: Qn, preset
  D_Flip_Flop d_ff_15 (.D(multiplexer_13_out), .clk(Clock), .Q(Out_14), .reset(Reset));  // open: Qn, preset
  D_Flip_Flop d_ff_16 (.D(multiplexer_14_out), .clk(Clock), .Q(Out_15), .reset(Reset));  // open: Qn, preset
endmodule
